# Fritzing sketch Untitled Sketch 2 (saved by Fritzing 0.9.3b)

parts:
  esp1 = ESP32 DevKitc V4
  Part1 = LCD1602-I2C
  U1 = LM2596 step down module  # not connected
  A1 = 2 channel relay module [package=THT]  # not connected
  DHT1 = Humidity and Temperature Sensor DHT11  # not connected
  Part2 = FC-28 Soil Hygrometer Module - Probe  # not connected
  Part3 = FC-28 Soil Hygrometer Module  # not connected
  M1 = DC Motor  # not connected

nets:
  N1: esp1.IO21, Part1.SDA
  N2: esp1.IO22, Part1.SCL
  GND: esp1.GND, Part1.GND
  5V: esp1.5V, Part1.VCC

custom parts:
  ESP32 DevKitc V4: ESP32-DevKitC board with ESP32-WROOM-32 module. ESP32-DevKitC V4 is a small-sized ESP32-based development board produced by Espressif. Most of the pins on the ESP module are broken out to the pin headers on the board. The pins D0, D1, D2, D3, CMD and CLK are used internally for communication between ESP32 and SPI flash memory. They are grouped on both sides near the USB connector. Avoid using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
  LCD1602-I2C: A standard character display, usually with 2x16 characters. Comes in many colors with LCM1602 IIC attached.
  LM2596 step down module: LM2596 DC-DC step down power supply module 3 A.
  2 channel relay module: 2 channel Relay Module 5V 12V 24V High and Low Level Trigger Relay Control With Optocoupler Two Way relays DC 5 V 12 V 24 V Volt.
  Humidity and Temperature Sensor DHT11: Digital relative humidity & temperature sensor DHT11
  FC-28 Soil Hygrometer Module - Probe: The FC-28 is a soil hygrometer module that uses the Texas Instruments LM393 comparator chip to provide an analog measurement of soil humidity.
  FC-28 Soil Hygrometer Module: The FC-28 is a soil hygrometer module that uses the Texas Instruments LM393 comparator chip to provide an analog measurement of soil humidity. The digital output is high when soil moisture is over a certain threshold, as determined by adjusting the potentiometer.
