# Fritzing sketch Wiring Tanaman (saved by Fritzing 0.9.3b)

parts:
  esp1 = ESP32 DevKitc V4
  Part1 = LCD1602-I2C
  U1 = LM2596 step down module
  A1 = 2 channel relay module [package=THT]
  DHT1 = Humidity and Temperature Sensor DHT11
  Part2 = FC-28 Soil Hygrometer Module - Probe
  Part3 = FC-28 Soil Hygrometer Module
  BAT1 = 12 battery [package=battery]
  M1 = DC Motor
  M2 = DC Motor

nets:
  N1: esp1.IO18, A1.pin_15
  N2: esp1.IO19, A1.pin_16
  N3: esp1.GND#12, U1.IN-, U1.OUT-, A1.pin_14, BAT1.-
  N4: esp1.IO21, Part1.SDA
  N5: esp1.IO22, Part1.SCL
  N6: esp1.IO23, DHT1.Data-signal
  N7: esp1.GND#18, Part1.GND, DHT1.GND_1
  VCC: esp1.3V3, DHT1.Vcc, Part3.VCC
  N8: esp1.IO34, Part3.AO
  N9: esp1.GND#32, Part3.GND
  5V: esp1.5V, Part1.VCC, U1.OUT+
  N10: U1.IN+, A1.pin_13, BAT1.+
  N11: A1.pin_5, M1.pin_2, M2.pin_2
  N12: A1.pin_6, M1.pin_1, M2.pin_1
  N13: Part2.POS, Part3.POS
  N14: Part2.NEG, Part3.NEG

custom parts:
  ESP32 DevKitc V4: ESP32-DevKitC board with ESP32-WROOM-32 module. ESP32-DevKitC V4 is a small-sized ESP32-based development board produced by Espressif. Most of the pins on the ESP module are broken out to the pin headers on the board. The pins D0, D1, D2, D3, CMD and CLK are used internally for communication between ESP32 and SPI flash memory. They are grouped on both sides near the USB connector. Avoid using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
  LCD1602-I2C: A standard character display, usually with 2x16 characters. Comes in many colors with LCM1602 IIC attached.
  LM2596 step down module: LM2596 DC-DC step down power supply module 3 A.
  2 channel relay module: 2 channel Relay Module 5V 12V 24V High and Low Level Trigger Relay Control With Optocoupler Two Way relays DC 5 V 12 V 24 V Volt.
  Humidity and Temperature Sensor DHT11: Digital relative humidity & temperature sensor DHT11
  FC-28 Soil Hygrometer Module - Probe: The FC-28 is a soil hygrometer module that uses the Texas Instruments LM393 comparator chip to provide an analog measurement of soil humidity.
  FC-28 Soil Hygrometer Module: The FC-28 is a soil hygrometer module that uses the Texas Instruments LM393 comparator chip to provide an analog measurement of soil humidity. The digital output is high when soil moisture is over a certain threshold, as determined by adjusting the potentiometer.
  12 battery: 12V lead acid type battery, like the Husqvarna YTH2448 12V 35AH battery. This is the mini version 1/4 the size of the actual battery to be closer to typical breadboard parts (around 2in wide rathher than 7in). The pads in pcb are sized to accomidate up to 14ga wire (as these batterys will deliver high currents.)
